# Fritzing sketch fritzing circuit (saved by Fritzing 0.9.4)

parts:
  Part3 = Arduino Uno (Rev3)
  BAT3 = BC9VPC [package=bc9vpc]
  M13 = DC Motor
  M14 = DC Motor
  M11 = L293D Motor Driver
  HC-SR04_Sensor_1 = HC-SR04 Ultrasonic Distance Sensor
  J1 = Basic Servo

nets:
  N1: Part3.D8, HC-SR04_Sensor_1.TRIG
  N2: Part3.D9_PWM, J1.pulse
  N3: Part3.D10_PWM/SS, M11.pin_5
  N4: Part3.D11_PWM/MOSI, M11.pin_6
  N5: Part3.D12/MISO, M11.pin_7
  N6: Part3.D13/SCK, M11.pin_8
  GND: Part3.GND, BAT3.V-, HC-SR04_Sensor_1.GND, J1.gnd
  N7: Part3.D7, HC-SR04_Sensor_1.ECHO
  5V: Part3.5V, HC-SR04_Sensor_1.VCC
  N8: Part3.VIN, BAT3.V+
  N9: M13.pin_1, M11.pin_11
  N10: M13.pin_2, M11.pin_12
  N11: M14.pin_1, M11.pin_9
  N12: M14.pin_2, M11.pin_10
